# Fritzing sketch speed (saved by Fritzing 0.8.7b)
breadboards: 1

parts:
  Part1 = EasyDriver_v44
  M1 = Stepper Motor - Bipolar
  Part2 = Arduino Nano (Rev3.0)  # not connected
  VCC1 = Battery block 9V
  S1 = Pushbutton [package=THT]  # not connected

nets:
  N1: Part1.GND, VCC1.-
  N2: Part1.V+, VCC1.+
  N3: Part1.OUT2A, M1.A
  N4: Part1.OUT2B, M1.C
  N5: Part1.OUT1A, M1.B
  N6: Part1.OUT1B, M1.D

notes:
  9-12 VDC Supply (do NOT use a 9V battery as shown)
  Normally Open (N/O) Pulse Sense Circuit.  Push-Buttton shown for demonstration
